// Logisim project my_CPU.circ as structural Verilog
module PC (
  input  [31:0] Pc_input,
  input  Write_enable,
  input  Clock,
  output [31:0] Pc_ouput
);

  Register #(.width(32)) register_1 (.D(Pc_input), .en(Write_enable), .clk(Clock), .Q(Pc_ouput));  // open: clr
endmodule

module PC_complete (
  input  [31:0] input_plus_1,
  input  [31:0] input_plus_n,
  input  [31:0] input_reset,
  input  [31:0] in_4,
  input  [1:0] select_input,
  input  Write_enable,
  input  Clock,
  output [31:0] Pc_val
);

  wire [31:0] multiplexer_1_out;

  Multiplexer #(.select(2), .width(32)) multiplexer_1 (
    .in0(input_plus_1), .in1(input_plus_n), .in2(input_reset), .in3(in_4), .out(multiplexer_1_out),
    .sel(select_input));
  PC pc_1 (.Pc_input(multiplexer_1_out), .Write_enable(Write_enable), .Clock(Clock), .Pc_ouput(Pc_val));
endmodule

module ALU (
  input  [31:0] A,
  input  [31:0] B,
  output [31:0] Carry,
  output [31:0] add,
  output [31:0] Borrow,
  output [31:0] subtract,
  output [31:0] shift_left_logic,
  output [31:0] shift_right_logic,
  output [31:0] shift_right_arithmetic,
  output [31:0] A_and_B,
  output [31:0] A_or_B,
  output [31:0] A_xor_B,
  output [31:0] slt,
  output [31:0] sltu
);

  wire adder_1_cout, comparator_1_lt, comparator_2_lt, subtractor_1_bout;

  Adder #(.width(32)) adder_1 (.a(A), .b(B), .out(add), .cin(1'b0), .cout(adder_1_cout));
  Subtractor #(.width(32)) subtractor_1 (.a(A), .b(B), .out(subtract), .bin(1'b0), .bout(subtractor_1_bout));
  Shifter #(.width(32)) shifter_1 (.in(A), .\dist (B[4:0]), .out(shift_left_logic));
  Shifter #(.shift("lr"), .width(32)) shifter_2 (.in(A), .\dist (B[4:0]), .out(shift_right_logic));
  Shifter #(.shift("ar"), .width(32)) shifter_3 (.in(A), .\dist (B[4:0]), .out(shift_right_arithmetic));
  assign A_and_B = A & B;  // AND_Gate and_1, 32 bits wide
  assign A_or_B = A | B;  // OR_Gate or_1, 32 bits wide
  assign A_xor_B = A ^ B;  // XOR_Gate xor_1, 32 bits wide
  Comparator #(.width(32)) comparator_1 (.a(A), .b(B), .lt(comparator_1_lt));  // open: gt, eq
  Comparator #(.mode("unsigned"), .width(32)) comparator_2 (.a(A), .b(B), .lt(comparator_2_lt));  // open: gt, eq
  Multiplexer #(.width(32)) multiplexer_1 (.in0({32{1'b0}}), .in1(32'h1), .out(Carry), .sel(adder_1_cout));
  Multiplexer #(.width(32)) multiplexer_2 (.in0({32{1'b0}}), .in1(32'h1), .out(Borrow), .sel(subtractor_1_bout));
  Multiplexer #(.width(32)) multiplexer_3 (.in0({32{1'b0}}), .in1(32'h1), .out(slt), .sel(comparator_1_lt));
  Multiplexer #(.width(32)) multiplexer_4 (.in0({32{1'b0}}), .in1(32'h1), .out(sltu), .sel(comparator_2_lt));
endmodule

module ALU_complete (
  input  [31:0] A,
  input  [31:0] B,
  input  [3:0] op,
  output [31:0] out_4
);

  wire decoder_1_out0, decoder_1_out1, decoder_1_out2, decoder_1_out3, decoder_1_out4, decoder_1_out5,
       decoder_1_out6, decoder_1_out7, decoder_1_out8, decoder_1_out9;
  wire [31:0] alu_1_a_and_b, alu_1_a_or_b, alu_1_a_xor_b, alu_1_add, alu_1_shift_left_logic,
       alu_1_shift_right_arithmetic, alu_1_shift_right_logic, alu_1_slt, alu_1_sltu, alu_1_subtract;

  Decoder #(.enable("false"), .select(4)) decoder_1 (
    .out0(decoder_1_out0), .out1(decoder_1_out1), .out2(decoder_1_out2), .out3(decoder_1_out3),
    .out4(decoder_1_out4), .out5(decoder_1_out5), .out6(decoder_1_out6), .out7(decoder_1_out7),
    .out8(decoder_1_out8), .out9(decoder_1_out9), .sel(op));  // open: out10, out11, out12, out13, out14, out15
  ALU alu_1 (
    .A(A), .B(B), .add(alu_1_add), .subtract(alu_1_subtract), .shift_left_logic(alu_1_shift_left_logic),
    .shift_right_logic(alu_1_shift_right_logic), .shift_right_arithmetic(alu_1_shift_right_arithmetic),
    .A_and_B(alu_1_a_and_b), .A_or_B(alu_1_a_or_b), .A_xor_B(alu_1_a_xor_b), .slt(alu_1_slt),
    .sltu(alu_1_sltu));  // open: Carry, Borrow
  assign out_4 = decoder_1_out9 ? alu_1_sltu : 32'bz;  // Controlled_Buffer controlled_buffer_1
  assign out_4 = decoder_1_out5 ? alu_1_a_and_b : 32'bz;  // Controlled_Buffer controlled_buffer_2
  assign out_4 = decoder_1_out6 ? alu_1_a_or_b : 32'bz;  // Controlled_Buffer controlled_buffer_3
  assign out_4 = decoder_1_out7 ? alu_1_a_xor_b : 32'bz;  // Controlled_Buffer controlled_buffer_4
  assign out_4 = decoder_1_out8 ? alu_1_slt : 32'bz;  // Controlled_Buffer controlled_buffer_5
  assign out_4 = decoder_1_out2 ? alu_1_shift_left_logic : 32'bz;  // Controlled_Buffer controlled_buffer_6
  assign out_4 = decoder_1_out3 ? alu_1_shift_right_logic : 32'bz;  // Controlled_Buffer controlled_buffer_7
  assign out_4 = decoder_1_out4 ? alu_1_shift_right_arithmetic : 32'bz;  // Controlled_Buffer controlled_buffer_8
  assign out_4 = decoder_1_out0 ? alu_1_add : 32'bz;  // Controlled_Buffer controlled_buffer_9
  assign out_4 = decoder_1_out1 ? alu_1_subtract : 32'bz;  // Controlled_Buffer controlled_buffer_10
endmodule

module general_register_group (
  input  [4:0] Address_5_bit,
  input  Write_enbale,
  input  Output_enable,
  input  Clock,
  input  [31:0] Data_input,
  output [31:0] Data_output
);

  RAM #(.addrWidth(5), .dataWidth(32)) Register_group (
    .addr(Address_5_bit), .we(Write_enbale), .oe(Output_enable), .clk(Clock), .din(Data_input),
    .dout(Data_output));
endmodule

module instruction_decoder (
  input  [31:0] instruction
);

  instruction_stuct_decoder instruction_stuct_decoder_1 (.instruction(instruction));  // open: opcode, rd, rs1, rs2, funct3, funct7, I_11_0, S_11_0, B_12_1_0, U_31_12, J_20_1_0
endmodule

module instruction_stuct_decoder (
  input  [31:0] instruction,
  output [6:0] opcode,
  output [4:0] rd,
  output [4:0] rs1,
  output [4:0] rs2,
  output [2:0] funct3,
  output [6:0] funct7,
  output [11:0] I_11_0,
  output [11:0] S_11_0,
  output [12:0] B_12_1_0,
  output [19:0] U_31_12,
  output [12:0] J_20_1_0
);


  assign B_12_1_0 = {instruction[31], instruction[7], instruction[30:25], instruction[11:8], 1'b0};
  assign funct3 = instruction[14:12];
  assign funct7 = instruction[31:25];
  assign I_11_0 = instruction[31:20];
  assign opcode = instruction[6:0];
  assign rd = instruction[11:7];
  assign rs1 = instruction[19:15];
  assign rs2 = instruction[24:20];
  assign S_11_0 = {instruction[31:25], instruction[11:7]};
  assign U_31_12 = instruction[31:12];
endmodule
